# Fritzing sketch sensEAT_2 (saved by Fritzing 0.9.2b)
breadboards: 1

parts:
  2_Kg_Load_Cell = Load Cell - Red/white/black/green
  Weight_Measurement_Sensor_HX711 = HX711 Weighing Sensor Module
  Eleman2 = Arduino Mega ADK (Rev3)
  100K_Thermistor = Temperature Sensor (Thermistor) [thermistor_type=NTC package=THT]
  R3 = Resistor [tolerance=±5% resistance=100k package="0603 [SMD]"]
  ECG_Sensor = AD8232 HeartRate Monitor [part_number=AD8232 package="DIP (Dual Inline) [THT]"]
  EMG_Grove_Sensor = Grove Button

nets:
  N1: 2_Kg_Load_Cell.wire1, Weight_Measurement_Sensor_HX711.E+
  N2: 2_Kg_Load_Cell.wire2, Weight_Measurement_Sensor_HX711.E-
  N3: 2_Kg_Load_Cell.wire3, Weight_Measurement_Sensor_HX711.A+
  N4: 2_Kg_Load_Cell.wire4, Weight_Measurement_Sensor_HX711.A-
  VCC: Weight_Measurement_Sensor_HX711.VCC, Eleman2.5V, 100K_Thermistor.pin_0, EMG_Grove_Sensor.VCC
  GND: Weight_Measurement_Sensor_HX711.GND, Eleman2.GND, R3.Pin_0, ECG_Sensor.GND, EMG_Grove_Sensor.GND
  N5: Weight_Measurement_Sensor_HX711.DO/RX, Eleman2.D2_PWM
  N6: Weight_Measurement_Sensor_HX711.CK/TX, Eleman2.D3_PWM
  N7: Eleman2.A0, ECG_Sensor.OUTPUT
  N8: Eleman2.A1, 100K_Thermistor.pin_1, R3.Pin_1
  N9: Eleman2.A2, EMG_Grove_Sensor.SIG
  N10: Eleman2.D11_PWM, ECG_Sensor.LO-
  N11: Eleman2.D10_PWM, ECG_Sensor.LO+
  3V3: Eleman2.3V3, ECG_Sensor.3.3v

custom parts:
  Load Cell - Red/white/black/green: A rectangle load cell/weighting pressure Sensor with four wires - Red, white, black, green. Normally corresponding with E+, E-, A+, A- respectively.
  HX711 Weighing Sensor Module: HX711 is a precision 24-bit analog-to-digital converter (ADC) designed for weigh scales and industrial control applications to interface directly with a bridge sensor.
  AD8232 HeartRate Monitor: A DIP stand-in part for whatever IC you want. With 10 pins on a 600mil dual inline package (DIP) footprint.
