# Fritzing sketch sensEAT_fst (saved by Fritzing 0.9.2b)
breadboards: 1

parts:
  Eleman3 = Arduino Mega ADK (Rev3)
  2_Kg_Load_Cell = Load Cell - Red/white/black/green
  Weight_Measurement_Sensor_HX711 = HX711 Weighing Sensor Module
  R4 = Resistor [tolerance=±5% resistance=100k package="0603 [SMD]"]
  100K_Thermistor = Temperature Sensor (Thermistor) [thermistor_type=NTC package=THT]
  ECG_Sensor = AD8232 HeartRate Monitor [part_number=AD8232 chip_label=IC package="DIP (Dual Inline) [THT]"]
  Force_Sensitive_Resistor = Basic Force Sensing Resistor (FSR) [package=THT]
  R5 = Resistor [tolerance=±5% resistance=10k package="2010 [SMD]"]

nets:
  N1: Eleman3.A0, ECG_Sensor.OUTPUT
  N2: Eleman3.A1, R4.Pin_1, 100K_Thermistor.pin_1
  N3: Eleman3.A2, Force_Sensitive_Resistor.pin_1, R5.Pin_0
  N4: Eleman3.D11_PWM, ECG_Sensor.LO-
  N5: Eleman3.D10_PWM, ECG_Sensor.LO+
  3V3: Eleman3.3V3, ECG_Sensor.3.3v
  5V: Eleman3.5V, Weight_Measurement_Sensor_HX711.VCC, 100K_Thermistor.pin_0, Force_Sensitive_Resistor.pin_0
  GND: Eleman3.GND, Weight_Measurement_Sensor_HX711.GND, R4.Pin_0, ECG_Sensor.GND, R5.Pin_1
  N6: Eleman3.D2_PWM, Weight_Measurement_Sensor_HX711.DO/RX
  N7: Eleman3.D3_PWM, Weight_Measurement_Sensor_HX711.CK/TX
  N8: 2_Kg_Load_Cell.wire1, Weight_Measurement_Sensor_HX711.E+
  N9: 2_Kg_Load_Cell.wire2, Weight_Measurement_Sensor_HX711.E-
  N10: 2_Kg_Load_Cell.wire3, Weight_Measurement_Sensor_HX711.A+
  N11: 2_Kg_Load_Cell.wire4, Weight_Measurement_Sensor_HX711.A-

custom parts:
  Load Cell - Red/white/black/green: A rectangle load cell/weighting pressure Sensor with four wires - Red, white, black, green. Normally corresponding with E+, E-, A+, A- respectively.
  HX711 Weighing Sensor Module: HX711 is a precision 24-bit analog-to-digital converter (ADC) designed for weigh scales and industrial control applications to interface directly with a bridge sensor.
  AD8232 HeartRate Monitor: A DIP stand-in part for whatever IC you want. With 10 pins on a 600mil dual inline package (DIP) footprint.
